# Fritzing sketch Stairway proto (saved by Fritzing 0.9.2b)

parts:
  Q1 = Basic FET N-Channel [package="TO220 [THT]"]
  Q2 = Basic FET N-Channel [package="TO220 [THT]"]
  Q3 = Basic FET N-Channel [package="TO220 [THT]"]
  V1 = DC Power [voltage=12V]
  R1 = Resistor [tolerance=±5% resistance=10k package=THT]
  R2 = Resistor [tolerance=±5% resistance=10k package=THT]
  R3 = Resistor [tolerance=±5% resistance=10k package=THT]
  R4 = Photocell (LDR) [package=THT]
  R5 = Resistor [tolerance=±5% resistance=10k package=THT]
  R6 = Photocell (LDR) [package=THT]
  R7 = Resistor [tolerance=±5% resistance=10k package=THT]
  R8 = Photocell (LDR) [package=THT]
  R9 = Resistor [tolerance=±5% resistance=10k package=THT]
  R10 = Photocell (LDR) [package=THT]
  R11 = Photocell (LDR) [package=THT]
  R12 = Photocell (LDR) [package=THT]
  R13 = Resistor [tolerance=±5% resistance=10k package=THT]
  R14 = Resistor [tolerance=±5% resistance=10k package=THT]
  R15 = Resistor [tolerance=±5% resistance=10k package=THT]
  Part1 = Arduino Uno (Rev3)
  J1 = Infrared Proximity Sensor
  U1 = mystery part, 7 pins [chip_label=MB1040]
  Reset = Pushbutton [package="[THT]"]
  R16 = Resistor [tolerance=±20% resistance=10k package=THT]
  Override_On = Pushbutton [package="[THT]"]
  R17 = Resistor [tolerance=±5% resistance=10k package=THT]
  Part2 = Analog Digital MUX Breakout
  C1 = Electrolytic Capacitor [capacitance=10µF package="100 mil [THT, electrolytic]"]
  J2 = Infrared Proximity Sensor
  C2 = Electrolytic Capacitor [capacitance=10µF package="100 mil [THT, electrolytic]"]
  PIR1 = mystery part, 3 pins [chip_label=miniPIR]
  PIR2 = mystery part, 3 pins [chip_label=miniPIR]
  PIR3 = mystery part, 3 pins [chip_label=miniPIR]

nets:
  N1: Q1.gate, R1.Pin_1, Part1.D3_PWM
  LED Strip -: Q1.drain, Q2.drain, Q3.drain
  N2: Q1.source, Q2.source, Q3.source, V1.V-, R1.Pin_0, R2.Pin_0, R3.Pin_0, R5.Pin_0, R7.Pin_0, R9.Pin_0, R13.Pin_0, R14.Pin_0, R15.Pin_0, Part1.GND, R16.Pin_0, R17.Pin_0, PIR1.pin1, PIR2.pin1, PIR3.pin1
  N3: Q2.gate, R2.Pin_1, Part1.D5_PWM
  N4: Q3.gate, R3.Pin_1, Part1.D6_PWM
  LED Strip +: V1.V+, Part1.VIN
  N5: R4.pin_0, R5.Pin_1, Part2.C0
  VCC: R4.pin_1, R6.pin_1, R8.pin_1, R10.pin_1, R11.pin_1, R12.pin_1, Part1.5V, J1.Vcc, U1.pin2, Reset.Pin_1, Reset.Pin_2, Override_On.Pin_1, Override_On.Pin_2, Part2.VCC, C1.+, J2.Vcc, C2.+, PIR1.pin2, PIR2.pin2, PIR3.pin2
  N6: R6.pin_0, R7.Pin_1, Part2.C1
  N7: R8.pin_0, R9.Pin_1, Part2.C2
  N8: R10.pin_0, R13.Pin_1, Part2.C5
  N9: R11.pin_0, R14.Pin_1, Part2.C4
  N10: R12.pin_0, R15.Pin_1, Part2.C3
  N11: Part1.A0, Part1.D8, Part2.SIG
  N12: Part1.D9_PWM, Part2.S2
  N13: Part1.D10_PWM/SS, Part2.S3
  N14: Part1.D11_PWM/MOSI, Override_On.Pin_3, Override_On.Pin_4, R17.Pin_1
  N15: Part1.D12/MISO, Part2.S1
  N16: Part1.D13/SCK, Part2.S0
  N17: Part1.RESET, Reset.Pin_3, Reset.Pin_4, R16.Pin_1
  N18: J1.Vout, Part2.C6
  GND: J1.GND, U1.pin1, Part2.GND, Part2.EN, C1.-
  N19: U1.pin6, Part2.C15
  N20: Part2.C7, J2.Vout
  N21: Part2.C10, PIR1.pin3
  N22: Part2.C11, PIR2.pin3
  N23: Part2.C12, PIR3.pin3
  N24: J2.GND, C2.-
